# Fritzing sketch wiring-diagram (saved by Fritzing 0.9.3b)
breadboards: 1

parts:
  VCC1 = 4 x AAA Battery Mount
  J1 = Basic Servo
  J2 = Basic Servo
  Part1 = Tessel 2

nets:
  GND: VCC1.-, J1.gnd, J2.gnd, Part1.GND
  VCC: VCC1.+, J1.vcc, J2.vcc

custom parts:
  Tessel 2: Draft version of Tessel 2
